// Logisim project P3_L0_CPU.circ as structural Verilog: 11 circuits, main circuit main
module main (
  input  reset,
  output [31:0] out_2,
  output [31:0] out_3,
  output out_4,
  output [4:0] out_5,
  output [31:0] out_6,
  output out_7,
  output [31:0] out_8,
  output [31:0] out_9
);

  wire ALU_immIn, ALUzero, and_1_out, Branch, clk, high, jump, Mem2Reg, Reg2Rd, SignExt;
  wire [2:0] ALUctrl;
  wire [4:0] rd, rs, rt;
  wire [5:0] instrsplitter_1_func_5_0, instrsplitter_1_op_31_26;
  wire [15:0] _16bit_imm;
  wire [25:0] _26bit;
  wire [31:0] adder_1_out, alu_1_result, bit_extender_1_out, bit_extender_2_out, bit_extender_3_out, MemRead,
       multiplexer_3_out, multiplexer_4_out, multiplexer_6_out, PC_4, PC_next, Reg1, shifter_1_out,
       shifter_2_out;

  Clock clock_1 (.out(clk));
  // Probe on out_3
  Multiplexer #(.width(5)) multiplexer_1 (.in0(rt), .in1(rd), .out(out_5), .sel(Reg2Rd));  // open: en
  Multiplexer #(.width(32)) multiplexer_2 (.in0(out_8), .in1(MemRead), .out(out_6), .sel(Mem2Reg));  // open: en
  // Probe on out_6
  // Probe on out_2
  GRF grf_1 (.A1(rs), .A2(rt), .A3(out_5), .WD(out_6), .WE(out_4), .RD1(Reg1), .clk(clk), .reset(reset), .RD2(out_9));
  IFU IFU (.PC_next(PC_next), .clk(clk), .reset(reset), .Instruct(out_2), .PC(out_3), .PC_4(PC_4));
  InstrSplitter instrsplitter_1 (
    .in_1(out_2), .Op_31_26(instrsplitter_1_op_31_26), .Rs_25_21(rs), .Rt_20_16(rt), .Rd_15_11(rd),
    .Func_5_0(instrsplitter_1_func_5_0), ._26bit_25_0(_26bit), ._16bit_15_0(_16bit_imm));  // open: Shamt_10_6
  assign bit_extender_1_out = {{16{1'b0}}, _16bit_imm};  // Bit_Extender bit_extender_1
  assign bit_extender_2_out = {{16{_16bit_imm[15]}}, _16bit_imm};  // Bit_Extender bit_extender_2
  Multiplexer #(.width(32)) multiplexer_3 (
    .in0(bit_extender_1_out), .in1(bit_extender_2_out), .out(multiplexer_3_out), .sel(SignExt));  // open: en
  Controller controller_1 (
    .op(instrsplitter_1_op_31_26), .\function (instrsplitter_1_func_5_0), .Reg2Rd(Reg2Rd),
    .ALUimm(ALU_immIn), .Mem2Reg(Mem2Reg), .RegWrite(out_4), .MemWrite(out_7), .Branch(Branch),
    .SignExt(SignExt), .ALUctrl(ALUctrl), .high(high), .jump(jump));
  Multiplexer #(.width(32)) multiplexer_4 (
    .in0(out_9), .in1(multiplexer_3_out), .out(multiplexer_4_out), .sel(ALU_immIn));  // open: en
  ALU alu_1 (.A(Reg1), .B(multiplexer_4_out), .ALU_ctrl(ALUctrl), .result(alu_1_result), .zero(ALUzero));
  DM dm_1 (.Address(out_8), .Data(out_9), .MemWrite(out_7), .Read(MemRead), .clk(clk), .reset(reset));
  Shifter #(.width(32)) shifter_1 (.in(alu_1_result), .\dist (5'b10000), .out(shifter_1_out));
  assign bit_extender_3_out = {{16{_16bit_imm[15]}}, _16bit_imm};  // Bit_Extender bit_extender_3
  Multiplexer #(.width(32)) multiplexer_5 (
    .in0(alu_1_result), .in1(shifter_1_out), .out(out_8), .sel(high));  // open: en
  Shifter #(.width(32)) shifter_2 (.in(bit_extender_3_out), .\dist (5'b00010), .out(shifter_2_out));
  // Probe on PC_4
  // Probe on adder_1_out
  Adder #(.width(32)) adder_1 (.a(PC_4), .b(shifter_2_out), .out(adder_1_out));  // open: cin, cout
  Multiplexer #(.width(32)) multiplexer_6 (
    .in0(PC_4), .in1(adder_1_out), .out(multiplexer_6_out), .sel(and_1_out));  // open: en
  and and_1 (and_1_out, ALUzero, Branch);
  Multiplexer #(.width(32)) multiplexer_7 (
    .in0(multiplexer_6_out), .in1({PC_4[31:28], _26bit, 2'b00}), .out(PC_next), .sel(jump));  // open: en

  // Other names for the same wires on the sheet: Instr[31:0] = out_2; ALUresult[31:0] = out_8; MemAddr[31:0] = out_8;
  //   MemWrite = out_7; PC[31:0] = out_3; MemData[31:0] = out_9; Reg2[31:0] = out_9; RegAddr[4:0] = out_5;
  //   RegData[31:0] = out_6; RegWrite = out_4
endmodule

module GRF (
  input  [4:0] A1,
  input  [4:0] A2,
  input  [4:0] A3,
  input  [31:0] WD,
  input  clk,
  input  reset,
  input  WE,
  output [31:0] RD1,
  output [31:0] RD2
);

  RegisterSet registerset_1 (
    .WD(WD), .WE(WE), .RD1(RD1), .RD2(RD2), .A1(A1), .A2(A2), .A3(A3), .clk(clk), .reset(reset));
endmodule

module RegisterSet (
  input  [4:0] A1,
  input  [4:0] A2,
  input  [4:0] A3,
  input  [31:0] WD,
  input  WE,
  input  clk,
  input  reset,
  output [31:0] RD1,
  output [31:0] RD2
);

  wire WE0, WE1, WE2, WE3, WE4, WE5, WE6, WE7, WE8, WE9, WE10, WE11, WE12, WE13, WE14, WE15, WE16, WE17,
       WE18, WE19, WE20, WE21, WE22, WE23, WE24, WE25, WE26, WE27, WE28, WE29, WE30, WE31;
  wire [31:0] _0, _1, _2, _3, _4, _5, _6, _7, _8, _9, _10, _11, _12, _13, _14, _15, _16, _17, _18, _19, _20,
       _21, _22, _23, _24, _25, _26, _27, _28, _29, _30, _31;

  Demultiplexer #(.select(5)) demultiplexer_1 (
    .out0(WE0), .out1(WE1), .out2(WE2), .out3(WE3), .out4(WE4), .out5(WE5), .out6(WE6), .out7(WE7),
    .out8(WE8), .out9(WE9), .out10(WE10), .out11(WE11), .out12(WE12), .out13(WE13), .out14(WE14),
    .out15(WE15), .out16(WE16), .out17(WE17), .out18(WE18), .out19(WE19), .out20(WE20), .out21(WE21),
    .out22(WE22), .out23(WE23), .out24(WE24), .out25(WE25), .out26(WE26), .out27(WE27), .out28(WE28),
    .out29(WE29), .out30(WE30), .out31(WE31), .in(WE), .sel(A3));  // open: en
  Register #(.width(32)) u__0 (.D({32{1'b0}}), .en(WE0), .Q(_0), .clk(clk), .clr(reset));
  Register #(.width(32)) u__4 (.D(WD), .en(WE4), .Q(_4), .clk(clk), .clr(reset));
  Register #(.width(32)) u__8 (.D(WD), .en(WE8), .Q(_8), .clk(clk), .clr(reset));
  Register #(.width(32)) u__12 (.D(WD), .en(WE12), .Q(_12), .clk(clk), .clr(reset));
  Register #(.width(32)) u__16 (.D(WD), .en(WE16), .Q(_16), .clk(clk), .clr(reset));
  Register #(.width(32)) u__20 (.D(WD), .en(WE20), .Q(_20), .clk(clk), .clr(reset));
  Register #(.width(32)) u__24 (.D(WD), .en(WE24), .Q(_24), .clk(clk), .clr(reset));
  Register #(.width(32)) u__28 (.D(WD), .en(WE28), .Q(_28), .clk(clk), .clr(reset));
  Register #(.width(32)) u__1 (.D(WD), .en(WE1), .Q(_1), .clk(clk), .clr(reset));
  Register #(.width(32)) u__5 (.D(WD), .en(WE5), .Q(_5), .clk(clk), .clr(reset));
  Register #(.width(32)) u__9 (.D(WD), .en(WE9), .Q(_9), .clk(clk), .clr(reset));
  Register #(.width(32)) u__13 (.D(WD), .en(WE13), .Q(_13), .clk(clk), .clr(reset));
  Register #(.width(32)) u__17 (.D(WD), .en(WE17), .Q(_17), .clk(clk), .clr(reset));
  Register #(.width(32)) u__21 (.D(WD), .en(WE21), .Q(_21), .clk(clk), .clr(reset));
  Register #(.width(32)) u__25 (.D(WD), .en(WE25), .Q(_25), .clk(clk), .clr(reset));
  Register #(.width(32)) u__29 (.D(WD), .en(WE29), .Q(_29), .clk(clk), .clr(reset));
  Register #(.width(32)) u__2 (.D(WD), .en(WE2), .Q(_2), .clk(clk), .clr(reset));
  Register #(.width(32)) u__6 (.D(WD), .en(WE6), .Q(_6), .clk(clk), .clr(reset));
  Register #(.width(32)) u__10 (.D(WD), .en(WE10), .Q(_10), .clk(clk), .clr(reset));
  Register #(.width(32)) u__14 (.D(WD), .en(WE14), .Q(_14), .clk(clk), .clr(reset));
  Register #(.width(32)) u__18 (.D(WD), .en(WE18), .Q(_18), .clk(clk), .clr(reset));
  Register #(.width(32)) u__22 (.D(WD), .en(WE22), .Q(_22), .clk(clk), .clr(reset));
  Register #(.width(32)) u__26 (.D(WD), .en(WE26), .Q(_26), .clk(clk), .clr(reset));
  Register #(.width(32)) u__30 (.D(WD), .en(WE30), .Q(_30), .clk(clk), .clr(reset));
  Register #(.width(32)) u__3 (.D(WD), .en(WE3), .Q(_3), .clk(clk), .clr(reset));
  Register #(.width(32)) u__7 (.D(WD), .en(WE7), .Q(_7), .clk(clk), .clr(reset));
  Register #(.width(32)) u__11 (.D(WD), .en(WE11), .Q(_11), .clk(clk), .clr(reset));
  Register #(.width(32)) u__15 (.D(WD), .en(WE15), .Q(_15), .clk(clk), .clr(reset));
  Register #(.width(32)) u__19 (.D(WD), .en(WE19), .Q(_19), .clk(clk), .clr(reset));
  Register #(.width(32)) u__23 (.D(WD), .en(WE23), .Q(_23), .clk(clk), .clr(reset));
  Register #(.width(32)) u__27 (.D(WD), .en(WE27), .Q(_27), .clk(clk), .clr(reset));
  Register #(.width(32)) u__31 (.D(WD), .en(WE31), .Q(_31), .clk(clk), .clr(reset));
  Multiplexer #(.select(5), .width(32)) multiplexer_1 (
    .in0(_0), .in1(_1), .in2(_2), .in3(_3), .in4(_4), .in5(_5), .in6(_6), .in7(_7), .in8(_8), .in9(_9),
    .in10(_10), .in11(_11), .in12(_12), .in13(_13), .in14(_14), .in15(_15), .in16(_16), .in17(_17),
    .in18(_18), .in19(_19), .in20(_20), .in21(_21), .in22(_22), .in23(_23), .in24(_24), .in25(_25),
    .in26(_26), .in27(_27), .in28(_28), .in29(_29), .in30(_30), .in31(_31), .out(RD1), .sel(A1));  // open: en
  Multiplexer #(.select(5), .width(32)) multiplexer_2 (
    .in0(_0), .in1(_1), .in2(_2), .in3(_3), .in4(_4), .in5(_5), .in6(_6), .in7(_7), .in8(_8), .in9(_9),
    .in10(_10), .in11(_11), .in12(_12), .in13(_13), .in14(_14), .in15(_15), .in16(_16), .in17(_17),
    .in18(_18), .in19(_19), .in20(_20), .in21(_21), .in22(_22), .in23(_23), .in24(_24), .in25(_25),
    .in26(_26), .in27(_27), .in28(_28), .in29(_29), .in30(_30), .in31(_31), .out(RD2), .sel(A2));  // open: en
endmodule

module IFU (
  input  [31:0] PC_next,
  input  clk,
  input  reset,
  output [31:0] Instruct,
  output [31:0] PC,
  output [31:0] PC_4
);

  PC u_PC (.PC_next(PC_next), .clk(clk), .reset(reset), .PC(PC), .PC_4(PC_4));
  IM IM (.PC(PC), .Instruct(Instruct));
endmodule

module IM (
  input  [31:0] PC,
  output [31:0] Instruct
);

  wire [31:0] subtractor_1_out;

  // Probe on PC
  Subtractor #(.width(32)) subtractor_1 (.a(PC), .b(32'h3000), .out(subtractor_1_out));  // open: bin, bout
  // Probe on subtractor_1_out[13:2]
  // Probe on Instruct
  ROM #(.addrWidth(12), .dataWidth(32)) rom_1 (.addr(subtractor_1_out[13:2]), .data(Instruct));  // open: sel

  // Notes on the sheet:
  //   contents of rom_1 (hex, n*v repeats v):
  //   341c0000 341d0000 34013456 210820 8c010004 ac010004 3c027878 411822 3c051234 34040005 0 ac85ffff
  //   8c83ffff 10650001 1000000d 34670404 10e3000b 0 3c087777 3508ffff 80022 34001100 e65020 34080000
  //   34090001 340a0001 10a4020 1109fffe 1000ffff
endmodule

module PC (
  input  [31:0] PC_next,
  input  clk,
  input  reset,
  output [31:0] PC,
  output [31:0] PC_4
);

  wire comparator_1_eq;
  wire [31:0] PC_q;

  Register #(.width(32)) u_PC (.D(PC_next), .Q(PC_q), .clk(clk), .clr(reset));  // open: en
  Multiplexer #(.width(32)) multiplexer_1 (.in0(PC_q), .in1(32'h3000), .out(PC), .sel(comparator_1_eq));  // open: en
  Comparator #(.width(32)) comparator_1 (.a(PC_q), .b({32{1'b0}}), .eq(comparator_1_eq));  // open: gt, lt
  // Probe on PC
  Adder #(.width(32)) adder_1 (.a(PC), .b(32'h4), .out(PC_4));  // open: cin, cout
endmodule

module ALU (
  input  [31:0] A,
  input  [31:0] B,
  input  [2:0] ALU_ctrl,
  output zero,
  output [31:0] result
);

  wire comparator_1_eq, comparator_2_eq;
  wire [31:0] add, \and , \or , sub;

  Adder #(.width(32)) adder_1 (.a(A), .b(B), .out(add));  // open: cin, cout
  Subtractor #(.width(32)) subtractor_1 (.a(A), .b(B), .out(sub));  // open: bin, bout
  assign \or  = A | B;  // OR_Gate or_1, 32 bits wide
  assign \and  = A & B;  // AND_Gate and_1, 32 bits wide
  Comparator #(.width(3)) comparator_1 (.a(ALU_ctrl), .b(3'b001), .eq(comparator_1_eq));  // open: gt, lt
  Comparator #(.width(32)) comparator_2 (.a({32{1'b0}}), .b(result), .eq(comparator_2_eq));  // open: gt, lt
  Multiplexer #(.select(3), .width(32)) multiplexer_1 (
    .in0(add), .in1(sub), .in2(\or ), .in3(\and ), .out(result), .sel(ALU_ctrl));  // open: in4, in5, in6, in7, en
  and and_2 (zero, comparator_1_eq, comparator_2_eq);
endmodule

module InstrSplitter (
  input  [31:0] in_1,
  output [5:0] Op_31_26,
  output [4:0] Rs_25_21,
  output [4:0] Rt_20_16,
  output [4:0] Rd_15_11,
  output [4:0] Shamt_10_6,
  output [5:0] Func_5_0,
  output [15:0] _16bit_15_0,
  output [25:0] _26bit_25_0
);


  assign _16bit_15_0 = in_1[15:0];
  assign _26bit_25_0 = in_1[25:0];
  assign Func_5_0 = in_1[5:0];
  assign Op_31_26 = in_1[31:26];
  assign Rd_15_11 = in_1[15:11];
  assign Rs_25_21 = in_1[25:21];
  assign Rt_20_16 = in_1[20:16];
  assign Shamt_10_6 = in_1[10:6];
endmodule

module Controller (
  input  [5:0] op,
  input  [5:0] \function ,
  output Reg2Rd,
  output ALUimm,
  output Mem2Reg,
  output RegWrite,
  output MemWrite,
  output Branch,
  output SignExt,
  output [2:0] ALUctrl,
  output high,
  output jump
);

  wire add, add_2_out, \and , and_2_out, beq, j, lui, lw, not_1_out, not_2_out, not_3_out, not_4_out,
       not_5_out, not_6_out, not_7_out, not_8_out, not_9_out, not_10_out, not_11_out, not_12_out, \or ,
       or_11_out, ori, special, sub, sub_2_out, sw;

  not not_1 (not_1_out, op[5]);
  not not_2 (not_2_out, op[4]);
  not not_3 (not_3_out, op[2]);
  not not_4 (not_4_out, op[3]);
  not not_5 (not_5_out, op[0]);
  not not_6 (not_6_out, op[1]);
  not not_7 (not_7_out, \function [5]);
  not not_8 (not_8_out, \function [4]);
  not not_9 (not_9_out, \function [2]);
  not not_10 (not_10_out, \function [3]);
  not not_11 (not_11_out, \function [0]);
  not not_12 (not_12_out, \function [1]);
  and u_special (special, not_5_out, not_6_out, not_3_out, not_4_out, not_2_out, not_1_out);
  and u_add (add, \function [5], not_8_out, not_10_out, special, not_9_out, not_12_out, not_11_out);
  and u_sub (sub, \function [5], not_8_out, not_10_out, special, not_9_out, \function [1], not_11_out);
  and u_or (\or , \function [5], not_8_out, not_10_out, special, \function [2], not_12_out, \function [0]);
  and u_and (\and , \function [5], not_8_out, not_10_out, special, \function [2], not_12_out, not_11_out);
  and u_ori (ori, not_1_out, not_2_out, op[3], op[2], not_6_out, op[0]);
  and u_lw (lw, op[5], not_2_out, not_4_out, not_3_out, op[1], op[0]);
  and u_sw (sw, op[5], not_2_out, op[3], not_3_out, op[1], op[0]);
  and u_beq (beq, not_1_out, not_2_out, not_4_out, op[2], not_6_out, not_5_out);
  and u_lui (lui, not_1_out, not_2_out, op[3], op[2], op[1], op[0]);
  and u_j (j, not_1_out, not_2_out, not_4_out, not_3_out, op[1], not_5_out);
  or or_2 (Reg2Rd, add, sub);
  or or_3 (ALUimm, ori, lw, sw, lui);
  buf or_4 (Mem2Reg, lw);  // OR_Gate
  or or_5 (RegWrite, add, sub, ori, lw, lui);
  buf or_6 (MemWrite, sw);  // OR_Gate
  buf or_7 (Branch, beq);  // OR_Gate
  or or_8 (SignExt, lw, sw);
  buf or_9 (high, lui);  // OR_Gate
  buf or_10 (jump, j);  // OR_Gate
  or add_2 (add_2_out, add, lw, sw);
  or sub_2 (sub_2_out, sub, beq);
  or or_11 (or_11_out, ori, lui);
  // OR_Gate and_2 has open pins: out=and_2_out
  ALUctrl aluctrl_1 (
    .add(add_2_out), .sub(sub_2_out), .\or (or_11_out), .\and (and_2_out), .ctrl2(ALUctrl[1]),
    .ctrl1(ALUctrl[0]));  // open: ctrl3

  assign ALUctrl[2] = 1'b0;
endmodule

module ALUctrl (
  input  add,
  input  sub,
  input  \or ,
  input  \and ,
  output ctrl3,
  output ctrl2,
  output ctrl1
);

  wire not_1_out, not_2_out, not_3_out, not_4_out;

  not not_1 (not_1_out, add);
  and and_1 (ctrl2, not_1_out, not_2_out);
  not not_2 (not_2_out, sub);
  not not_3 (not_3_out, add);
  and and_2 (ctrl1, not_3_out, not_4_out);
  not not_4 (not_4_out, \or );
endmodule

module DM (
  input  [31:0] Address,
  input  [31:0] Data,
  input  MemWrite,
  input  clk,
  input  reset,
  output [31:0] Read
);

  wire [11:0] bit_extender_1_out;

  Bit_Extender #(.in_width(32), .out_width(12)) bit_extender_1 (.in(Address), .out(bit_extender_1_out));
  RAM #(.addrWidth(12), .dataWidth(32), .bus("separate")) ram_1 (
    .addr(bit_extender_1_out), .din(Data), .data(Read), .str(MemWrite), .clk(clk), .clr(reset));  // open: sel, ld
endmodule
